# Fritzing sketch schematic (saved by Fritzing 0.9.3b)

parts:
  Raspberry_Pi_1 = Raspberry Pi 3 [part_number=RPI-3-V1.2]
  LED1 = LED - 3mm [color="Red (633nm)" package="3 mm [THT]"]
  R1 = Resistor [tolerance=±5% resistance=10k package=THT]
  Part1 = Arduino Pro Mini v13

nets:
  GND: Raspberry_Pi_1.GND, LED1.cathode, R1.Pin_1, Part1.GND
  N1: Raspberry_Pi_1.GIPO20, R1.Pin_0, Part1.D5_PWM
  N2: LED1.anode, Part1.D3_PWM
